# Fritzing sketch 3 led (saved by Fritzing 0.8.7b)
breadboards: 1

parts:
  U1 = NodeMCU V1.0
  LED1 = LED - 5mm [color="Red (633nm)" package="5 mm [THT]"]
  LED2 = LED - 5mm [color="Red (633nm)" package="5 mm [THT]"]
  LED3 = LED - 5mm [color="Red (633nm)" package="5 mm [THT]"]

nets:
  N1: U1.GND, LED1.cathode, LED2.cathode, LED3.cathode
  N2: U1.D5, LED3.anode
  N3: U1.D6, LED2.anode
  N4: U1.D7, LED1.anode

custom parts:
  NodeMCU V1.0: ESP8266 based NodeMCU
